// Logisim project RV32_IM.circ as structural Verilog: 2 circuits, main circuit main
module main (
);

  wire clock_1_out;
  wire [31:0] ADDR, DATA, INST, W_EN;

  Clock clock_1 (.out(clock_1_out));
  RAM #(.addrWidth(24), .dataWidth(32), .enables("line")) ram_1 (
    .addr(ADDR[23:0]), .we(clock_1_out), .clk(clock_1_out), .din(DATA), .dout(INST));
  CPU cpu_1 (.in_1(INST), .in_2(clock_1_out), .out_3(ADDR), .out_4(DATA), .out_5(W_EN));
endmodule

module CPU (
  input  [31:0] in_1,
  input  in_2,
  output [31:0] out_3,
  output [31:0] out_4,
  output [31:0] out_5
);

  wire [31:0] PC_1;

  Register #(.width(32)) PC (.D(PC_1), .en(in_2), .clk(in_2), .Q(out_3));  // open: clr
  Adder #(.width(32)) adder_1 (.a(out_3), .b(32'h1), .out(PC_1));  // open: cin, cout

  // Other names for the same wires on the sheet: CLK = in_2; PC[31:0] = out_3; RAM_ADDR[31:0] = out_3;
  //   RAM_DATA[31:0] = out_4; RAM_INSTRUCTION[31:0] = in_1; RAM_WRITE_EN[31:0] = out_5

  // Notes on the sheet:
  //   outputs
  //   I/O
  //   FETCH
  //   inputs
  //   DECODE
endmodule
